// Logisim project LogiSim_FullAdder_8Bit_2Zahlen.circ as structural Verilog: 1 circuit, main circuit main
module main (
  input  Bit8,
  input  Bit7,
  input  Bit6,
  input  Bit5,
  input  Bit4,
  input  Bit3,
  input  Bit2,
  input  Bit1,
  input  Bit8_2,
  input  Bit7_2,
  input  Bit6_2,
  input  Bit5_2,
  input  Bit4_2,
  input  Bit3_2,
  input  Bit2_2,
  input  Bit1_2,
  input  Carry0,
  output \Übertrag ,
  output Bit8_3,
  output Bit7_3,
  output Bit6_3,
  output Bit5_3,
  output Bit4_3,
  output Bit3_3,
  output Bit2_3,
  output Bit1_3
);

  wire and_1_out, and_2_out, and_3_out, and_4_out, and_5_out, and_6_out, and_7_out, and_8_out, and_9_out,
       and_10_out, and_11_out, and_12_out, and_13_out, and_14_out, and_15_out, and_16_out, or_1_out,
       or_2_out, or_3_out, or_4_out, or_5_out, or_6_out, or_7_out, or_8_out, xor_1_out, xor_2_out, xor_3_out,
       xor_4_out, xor_5_out, xor_6_out, xor_7_out, xor_8_out, xor_9_out, xor_10_out, xor_11_out, xor_12_out,
       xor_13_out, xor_14_out, xor_15_out, xor_16_out, \Übertrag_2_out , \Übertrag_3_out , \Übertrag_4_out ,
       \Übertrag_5_out , \Übertrag_6_out , \Übertrag_7_out , \Übertrag_out ;

  xor xor_1 (xor_1_out, Bit1, Bit1_2);
  and and_1 (and_1_out, Bit1, Bit1_2);
  xor xor_2 (xor_2_out, xor_1_out, Carry0);
  and and_2 (and_2_out, xor_1_out, Carry0);
  xor xor_3 (xor_3_out, Bit2, Bit2_2);
  and and_3 (and_3_out, Bit2, Bit2_2);
  xor xor_4 (xor_4_out, xor_3_out, \Übertrag_out );
  and and_4 (and_4_out, xor_3_out, \Übertrag_out );
  xor xor_5 (xor_5_out, Bit3, Bit3_2);
  and and_5 (and_5_out, Bit3, Bit3_2);
  xor xor_6 (xor_6_out, xor_5_out, \Übertrag_2_out );
  and and_6 (and_6_out, xor_5_out, \Übertrag_2_out );
  xor xor_7 (xor_7_out, Bit4, Bit4_2);
  and and_7 (and_7_out, Bit4, Bit4_2);
  xor xor_8 (xor_8_out, xor_7_out, \Übertrag_3_out );
  and and_8 (and_8_out, xor_7_out, \Übertrag_3_out );
  xor xor_9 (xor_9_out, Bit5, Bit5_2);
  and and_9 (and_9_out, Bit5, Bit5_2);
  xor xor_10 (xor_10_out, xor_9_out, \Übertrag_4_out );
  and and_10 (and_10_out, xor_9_out, \Übertrag_4_out );
  xor xor_11 (xor_11_out, Bit6, Bit6_2);
  and and_11 (and_11_out, Bit6, Bit6_2);
  xor xor_12 (xor_12_out, xor_11_out, \Übertrag_5_out );
  and and_12 (and_12_out, xor_11_out, \Übertrag_5_out );
  xor xor_13 (xor_13_out, Bit7, Bit7_2);
  and and_13 (and_13_out, Bit7, Bit7_2);
  xor xor_14 (xor_14_out, xor_13_out, \Übertrag_6_out );
  and and_14 (and_14_out, xor_13_out, \Übertrag_6_out );
  xor xor_15 (xor_15_out, Bit8, Bit8_2);
  and and_15 (and_15_out, Bit8, Bit8_2);
  xor xor_16 (xor_16_out, xor_15_out, \Übertrag_7_out );
  and and_16 (and_16_out, xor_15_out, \Übertrag_7_out );
  or or_1 (or_1_out, and_1_out, and_2_out);
  or or_2 (or_2_out, and_3_out, and_4_out);
  or or_3 (or_3_out, and_5_out, and_6_out);
  or or_4 (or_4_out, and_7_out, and_8_out);
  or or_5 (or_5_out, and_9_out, and_10_out);
  or or_6 (or_6_out, and_11_out, and_12_out);
  or or_7 (or_7_out, and_13_out, and_14_out);
  or or_8 (or_8_out, and_15_out, and_16_out);
  buf Sum (Bit1_3, xor_2_out);
  buf \u_Übertrag  (\Übertrag_out , or_1_out);
  buf Sum_2 (Bit2_3, xor_4_out);
  buf \u_Übertrag_2  (\Übertrag_2_out , or_2_out);
  buf Sum_3 (Bit3_3, xor_6_out);
  buf \u_Übertrag_3  (\Übertrag_3_out , or_3_out);
  buf Sum_4 (Bit4_3, xor_8_out);
  buf \u_Übertrag_4  (\Übertrag_4_out , or_4_out);
  buf Sum_5 (Bit5_3, xor_10_out);
  buf \u_Übertrag_5  (\Übertrag_5_out , or_5_out);
  buf Sum_6 (Bit6_3, xor_12_out);
  buf \u_Übertrag_6  (\Übertrag_6_out , or_6_out);
  buf Sum_7 (Bit7_3, xor_14_out);
  buf \u_Übertrag_7  (\Übertrag_7_out , or_7_out);
  buf Sum_8 (Bit8_3, xor_16_out);
  buf \u_Übertrag_8  (\Übertrag , or_8_out);

  // Notes on the sheet:
  //   Zahl A
  //   Zahl B
  //   Zahl AB
endmodule
